// Digital circuit digital_alarm_clock.dig as structural Verilog
module digital_alarm_clock (
  input  CLOCK
);

  wire AlarmEnabled, AlarmRinging, and_1_out, Key0, Key1, Key2, Key3, Key4, Key5, Key6, Key7, Key8, Key9,
       KeyEnter, KeyEsc, KeyMode, KeyReset, KeyToggleAlarm, Pulse, SetAlarmMode, SetTimeMode, TimeOfDayMode;
  wire [23:0] Display;

  integration Brain (
    .Reset(KeyReset), .Key0(Key0), .Key1(Key1), .Key2(Key2), .Key3(Key3), .Key4(Key4), .Key5(Key5),
    .Key6(Key6), .Key7(Key7), .Key8(Key8), .Key9(Key9), .KeyMode(KeyMode), .ToggleAlarm(KeyToggleAlarm),
    .KeyEnter(KeyEnter), .KeyEsc(KeyEsc), .CLK1024Hz(CLOCK), .Display(Display), .Pulse(Pulse),
    .TimeOfDayMode(TimeOfDayMode), .SetTimeMod(SetTimeMode), .SetAlarmMode(SetAlarmMode),
    .AlarmEnabled(AlarmEnabled), .AlarmRinging(AlarmRinging));
  Seven_Seg_Hex seven_seg_hex_1 (.d(Display[23:20]), .dp(1'b0));
  Button mode (.out(KeyMode));
  Button _1 (.out(Key1));
  Button _4 (.out(Key4));
  Button _7 (.out(Key7));
  Seven_Seg_Hex seven_seg_hex_2 (.d(Display[19:16]), .dp(1'b0));
  Button Enter (.out(KeyEnter));
  Button Alarm_Enable_Disable (.out(KeyToggleAlarm));
  Button _2 (.out(Key2));
  Button _5 (.out(Key5));
  Button _8 (.out(Key8));
  Button _0 (.out(Key0));
  Seven_Seg_Hex seven_seg_hex_3 (.d(Display[15:12]), .dp(1'b0));
  Seven_Seg_Hex seven_seg_hex_4 (.d(Display[11:8]), .dp(1'b0));
  Button Reset (.out(KeyReset));
  Button _3 (.out(Key3));
  Button _6 (.out(Key6));
  Button _9 (.out(Key9));
  Button ESC (.out(KeyEsc));
  Seven_Seg_Hex seven_seg_hex_5 (.d(Display[7:4]), .dp(1'b0));
  Seven_Seg_Hex seven_seg_hex_6 (.d(Display[3:0]), .dp(1'b0));
  and and_1 (and_1_out, Pulse, AlarmRinging);
  // MIDI midi_1: pin names not known; wires that end beside it: 7'b1100100, 7'b1100100, AlarmRinging, AlarmEnabled, Pulse
  LED led_1 (.in(TimeOfDayMode));
  LED led_2 (.in(SetTimeMode));
  LED led_3 (.in(SetAlarmMode));
  LED led_4 (.in(AlarmEnabled));
  LED led_5 (.in(and_1_out));

  // Other names for the same wires on the sheet: CLK_1024Hz = CLOCK

  // Notes on the sheet:
  //   CLOCK: Hz: 1024
  //   Display
  //   Keyboard
  //   Mode
  //   Alarm
endmodule
