// Digital circuit basic_clockv3.dig as structural Verilog
module basic_clockv3 (
  input  Clk,
  input  Reset,
  input  LD,
  input  [23:0] set_hhmmss,
  output [23:0] hhmmss,
  output FlashPulse
);

  wire _23_59_59, _23Hours, _59Min, _59Seconds, and_1_out, and_2_out, counterpreset_1_ovf,
       counterpreset_3_ovf, counterpreset_5_ovf, RESET_HH, SecondMarkerPulse;
  wire [8:0] PrescaleCount;

  Counter #(.Bits(10)) _1024To1 (
    .en(1'b1), .C(Clk), .clr(1'b0), .out({FlashPulse, PrescaleCount}), .ovf(SecondMarkerPulse));
  CounterPreset #(.maxValue(9), .Bits(4)) counterpreset_1 (
    .en(SecondMarkerPulse), .C(Clk), .dir(1'b0), .in(set_hhmmss[3:0]), .ld(LD), .clr(Reset),
    .out(hhmmss[3:0]), .ovf(counterpreset_1_ovf));
  CounterPreset #(.maxValue(5), .Bits(4)) counterpreset_2 (
    .en(counterpreset_1_ovf), .C(Clk), .dir(1'b0), .in(set_hhmmss[7:4]), .ld(LD), .clr(Reset),
    .out(hhmmss[7:4]));  // open: ovf
  and and_1 (and_1_out, _59Seconds, SecondMarkerPulse);
  and and_2 (and_2_out, _59Seconds, _59Min, SecondMarkerPulse);
  Seven_Seg_Hex seven_seg_hex_1 (.d(hhmmss[23:20]), .dp(1'b0));
  Seven_Seg_Hex seven_seg_hex_2 (.d(hhmmss[19:16]), .dp(1'b0));
  Seven_Seg_Hex seven_seg_hex_3 (.d(hhmmss[15:12]), .dp(1'b0));
  Seven_Seg_Hex seven_seg_hex_4 (.d(hhmmss[11:8]), .dp(1'b0));
  CounterPreset #(.maxValue(9), .Bits(4)) counterpreset_3 (
    .en(and_1_out), .C(Clk), .dir(1'b0), .in(set_hhmmss[11:8]), .ld(LD), .clr(Reset), .out(hhmmss[11:8]),
    .ovf(counterpreset_3_ovf));
  CounterPreset #(.maxValue(5), .Bits(4)) counterpreset_4 (
    .en(counterpreset_3_ovf), .C(Clk), .dir(1'b0), .in(set_hhmmss[15:12]), .ld(LD), .clr(Reset),
    .out(hhmmss[15:12]));  // open: ovf
  CounterPreset #(.maxValue(9), .Bits(4)) counterpreset_5 (
    .en(and_2_out), .C(Clk), .dir(1'b0), .in(set_hhmmss[19:16]), .ld(LD), .clr(RESET_HH),
    .out(hhmmss[19:16]), .ovf(counterpreset_5_ovf));
  CounterPreset #(.maxValue(2), .Bits(4)) counterpreset_6 (
    .en(counterpreset_5_ovf), .C(Clk), .dir(1'b0), .in(set_hhmmss[23:20]), .ld(LD), .clr(RESET_HH),
    .out(hhmmss[23:20]));  // open: ovf
  Seven_Seg_Hex seven_seg_hex_5 (.d(hhmmss[7:4]), .dp(1'b0));
  Seven_Seg_Hex seven_seg_hex_6 (.d(hhmmss[3:0]), .dp(1'b0));
  or or_1 (RESET_HH, Reset, _23_59_59);
  and and_3 (_23_59_59, _59Seconds, _59Min, _23Hours, SecondMarkerPulse);
  Comparator #(.Bits(8)) comparator_1 (.a(hhmmss[7:0]), .b(8'h59), .eq(_59Seconds));  // open: gt, lt
  Comparator #(.Bits(8)) comparator_2 (.a(hhmmss[15:8]), .b(8'h59), .eq(_59Min));  // open: gt, lt
  Comparator #(.Bits(8)) comparator_3 (.a(hhmmss[23:16]), .b(8'h23), .eq(_23Hours));  // open: gt, lt

  // Other names for the same wires on the sheet: Clk1024hz = Clk; Hours_1[3:0] = hhmmss[19:16];
  //   Hours_10[3:0] = hhmmss[23:20]; Minutes_1[3:0] = hhmmss[11:8]; Minutes_10[3:0] = hhmmss[15:12];
  //   PrescaleCount[9] = FlashPulse; Seconds_1[3:0] = hhmmss[3:0]; Seconds_10[3:0] = hhmmss[7:4];
  //   set_sec1[3:0] = set_hhmmss[3:0]; set_sec10[3:0] = set_hhmmss[7:4]; set_min1[3:0] = set_hhmmss[11:8];
  //   set_min10[3:0] = set_hhmmss[15:12]; set_hour1[3:0] = set_hhmmss[19:16]; set_hour10[3:0] = set_hhmmss[23:20]

  // Notes on the sheet:
  //   Clk: Hz: 1024
  //   Counters
  //   Comparators
endmodule
