// Digital circuit control.dig as structural Verilog
module control (
  input  [23:0] NewHHMMSS,
  input  [23:0] hhmmss,
  input  Clk,
  output [23:0] valid_HHMMSS,
  output valid
);

  wire gt_23Hours, gt_59Min, gt_59Seconds, invalid;
  wire [23:0] temp_hhmmss;

  Comparator #(.Bits(8)) comparator_1 (.a(NewHHMMSS[7:0]), .b(8'h59), .gt(gt_59Seconds));  // open: eq, lt
  Comparator #(.Bits(8)) comparator_2 (.a(NewHHMMSS[15:8]), .b(8'h59), .gt(gt_59Min));  // open: eq, lt
  Comparator #(.Bits(8)) comparator_3 (.a(NewHHMMSS[23:16]), .b(8'h23), .gt(gt_23Hours));  // open: eq, lt
  or or_1 (invalid, gt_23Hours, gt_59Min, gt_59Seconds);
  Multiplexer #(.Bits(4)) multiplexer_1 (
    .sel(invalid), .in_0(NewHHMMSS[23:20]), .in_1(temp_hhmmss[23:20]), .out(valid_HHMMSS[23:20]));
  Multiplexer #(.Bits(4)) multiplexer_2 (
    .sel(invalid), .in_0(NewHHMMSS[19:16]), .in_1(temp_hhmmss[19:16]), .out(valid_HHMMSS[19:16]));
  D_FF #(.Bits(24)) d_ff_1 (.D(hhmmss), .C(Clk), .Q(temp_hhmmss));  // open: nQ
  Multiplexer #(.Bits(4)) multiplexer_3 (
    .sel(invalid), .in_0(NewHHMMSS[15:12]), .in_1(temp_hhmmss[15:12]), .out(valid_HHMMSS[15:12]));
  // Probe on temp_hhmmss
  Multiplexer #(.Bits(4)) multiplexer_4 (
    .sel(invalid), .in_0(NewHHMMSS[11:8]), .in_1(temp_hhmmss[11:8]), .out(valid_HHMMSS[11:8]));
  Multiplexer #(.Bits(4)) multiplexer_5 (
    .sel(invalid), .in_0(NewHHMMSS[7:4]), .in_1(temp_hhmmss[7:4]), .out(valid_HHMMSS[7:4]));
  not not_1 (valid, invalid);
  Multiplexer #(.Bits(4)) multiplexer_6 (
    .sel(invalid), .in_0(NewHHMMSS[3:0]), .in_1(temp_hhmmss[3:0]), .out(valid_HHMMSS[3:0]));

  // Other names for the same wires on the sheet: Clk1024hz = Clk; set_sec1[3:0] = NewHHMMSS[3:0];
  //   set_sec10[3:0] = NewHHMMSS[7:4]; set_min1[3:0] = NewHHMMSS[11:8]; set_min10[3:0] = NewHHMMSS[15:12];
  //   set_hour1[3:0] = NewHHMMSS[19:16]; set_hour10[3:0] = NewHHMMSS[23:20]; temp_sec1[3:0] = temp_hhmmss[3:0];
  //   temp_sec10[3:0] = temp_hhmmss[7:4]; temp_min1[3:0] = temp_hhmmss[11:8]; temp_min10[3:0] = temp_hhmmss[15:12];
  //   temp_hour1[3:0] = temp_hhmmss[19:16]; temp_hour10[3:0] = temp_hhmmss[23:20];
  //   valid_set_hour1[3:0] = valid_HHMMSS[19:16]; valid_set_hour10[3:0] = valid_HHMMSS[23:20];
  //   valid_set_min1[3:0] = valid_HHMMSS[11:8]; valid_set_min10[3:0] = valid_HHMMSS[15:12];
  //   valid_set_sec1[3:0] = valid_HHMMSS[3:0]; valid_set_sec10[3:0] = valid_HHMMSS[7:4]

  // Notes on the sheet:
  //   Clk: Hz: 1024
  //   Comparators
  //   Validation
endmodule
