// Digital circuit integration.dig as structural Verilog
module integration (
  input  Reset,
  input  Key0,
  input  Key1,
  input  Key2,
  input  Key3,
  input  Key4,
  input  Key5,
  input  Key6,
  input  Key7,
  input  Key8,
  input  Key9,
  input  KeyMode,
  input  ToggleAlarm,
  input  KeyEnter,
  input  KeyEsc,
  input  CLK1024Hz,
  output [23:0] Display,
  output Pulse,
  output TimeOfDayMode,
  output SetTimeMod,
  output SetAlarmMode,
  output AlarmEnabled,
  output AlarmRinging
);

  wire AlarmMode, and_2_out, clrbuffer, comparator_1_eq, decoder_1_out_3, KeyCodeAvailable, ld_alarmreg,
       ld_timeofday, load, NumCodeAvaliable, SetMode, TimeOfDayMode_t, toggleAlarm_t, valid;
  wire [1:0] KeyCode, modes;
  wire [3:0] NumCode;
  wire [23:0] AlarmTime, hhmmss, New_valid_HHMMSS, NewHHMMSS, newTime_hhmmss, temp_time;

  // Probe on load
  and and_1 (load, valid, ld_timeofday);
  basic_clockv3 Clock_Functionality (
    .Clk(CLK1024Hz), .Reset(Reset), .LD(load), .set_hhmmss(New_valid_HHMMSS), .hhmmss(hhmmss),
    .FlashPulse(Pulse));
  keyboard_control Keyboard_Brain (
    ._0(Key0), ._1(Key1), ._2(Key2), ._3(Key3), ._4(Key4), ._5(Key5), ._6(Key6), ._7(Key7), ._8(Key8),
    ._9(Key9), .reset(Reset), .Alarm_EnableDisable(ToggleAlarm), .Enter(KeyEnter), .clrBuffer(clrbuffer),
    .Esc(KeyEsc), .NumCode(NumCode), .NumCodeAvailable(NumCodeAvaliable), .NewHHMMSS(NewHHMMSS),
    .KeyCode(KeyCode), .KeyCodeAvailable(KeyCodeAvailable));
  // Probe on KeyCode
  // Probe on NewHHMMSS
  Multiplexer #(.Selector_Bits(2), .Bits(24)) multiplexer_1 (
    .sel(modes), .in_0(hhmmss), .in_1(temp_time), .in_2(temp_time), .in_3({24{1'b0}}), .out(Display));
  // Probe on Display
  // Probe on KeyCode
  // Probe on KeyCodeAvailable
  // Probe on modes
  control Validation_Control (
    .NewHHMMSS(newTime_hhmmss), .hhmmss(hhmmss), .Clk(CLK1024Hz), .valid_HHMMSS(New_valid_HHMMSS),
    .valid(valid));
  Seven_Seg_Hex seven_seg_hex_1 (.d(Display[23:20]), .dp(1'b0));
  clock_time_alarm_controller #(.applicationType("IVERILOG"), .CodeFile("C:\\Users\\aykap\\Desktop\\digital_design\\proje\\verilog_modules\\clock_time_alarm_controller.v")) u_clock_time_alarm_controller (
    .clk(CLK1024Hz), .reset(Reset), .KeyCode(KeyCode), .KeyCodeAvailable(KeyCodeAvailable),
    .hhmmss(NewHHMMSS), .alarm_time(AlarmTime), .alarm_time_enabled(AlarmEnabled), .mode(modes),
    .temp_time(temp_time), .new_time_hhmmss(newTime_hhmmss), .ld_timeofdayreg(ld_timeofday),
    .ld_alarmreg(ld_alarmreg), .toggle_alarm(toggleAlarm_t), .clrBuffer(clrbuffer));
  Seven_Seg_Hex seven_seg_hex_2 (.d(Display[19:16]), .dp(1'b0));
  Seven_Seg_Hex seven_seg_hex_3 (.d(Display[15:12]), .dp(1'b0));
  Seven_Seg_Hex seven_seg_hex_4 (.d(Display[11:8]), .dp(1'b0));
  Seven_Seg_Hex seven_seg_hex_5 (.d(Display[7:4]), .dp(1'b0));
  Seven_Seg_Hex seven_seg_hex_6 (.d(Display[3:0]), .dp(1'b0));
  // Probe on clrbuffer
  // Probe on newTime_hhmmss
  // Probe on temp_time
  // Probe on ld_timeofday
  Decoder #(.Selector_Bits(2)) decoder_1 (
    .sel(modes), .out_0(TimeOfDayMode), .out_1(SetTimeMod), .out_2(SetAlarmMode), .out_3(decoder_1_out_3));
  CounterPreset #(.Bits(24)) u_AlarmTime (
    .en(1'b0), .C(CLK1024Hz), .dir(1'b0), .in(New_valid_HHMMSS), .ld(ld_alarmreg), .clr(Reset),
    .out(AlarmTime));  // open: ovf
  JK_FF_AS u_AlarmEnabled (
    .Set(1'b0), .J(ToggleAlarm), .C(ToggleAlarm), .K(ToggleAlarm), .Clr(Reset), .Q(AlarmEnabled));  // open: nQ
  LED time_of_day (.in(TimeOfDayMode));
  LED set_time_mode (.in(SetTimeMod));
  LED set_alarm_mode (.in(SetAlarmMode));
  // Probe on AlarmTime
  mode_control #(.applicationType("IVERILOG"), .CodeFile("C:\\Users\\aykap\\Desktop\\digital_design\\proje\\verilog_modules\\mode_control.v")) u_mode_control (
    .clk(KeyMode), .reset(Reset), .mode_button(KeyMode), .mode(modes));
  // Probe on modes
  Comparator #(.Bits(16)) comparator_1 (.a(AlarmTime[23:8]), .b(hhmmss[23:8]), .eq(comparator_1_eq));  // open: gt, lt
  Decoder #(.Selector_Bits(2)) decoder_2 (
    .sel(modes), .out_0(TimeOfDayMode_t), .out_1(SetMode), .out_2(AlarmMode));  // open: out_3
  and and_2 (and_2_out, Pulse, AlarmEnabled, comparator_1_eq);
  and and_3 (AlarmRinging, comparator_1_eq, AlarmEnabled);
  LED led_1 (.in(TimeOfDayMode_t));
  LED led_2 (.in(SetMode));
  LED led_3 (.in(AlarmMode));
  LED alarm (.in(and_2_out));
  // also tied to GND on the sheet: decoder_1_out_3

  // Other names for the same wires on the sheet: alarmEn = AlarmEnabled; CLK_1024Hz = CLK1024Hz; flashPulse = Pulse;
  //   KeyToggleAlarm = ToggleAlarm

  // Notes on the sheet:
  //   CLK1024Hz: Hz: 1024
  //   Validation
  //   Alarm
  //   Mode Control
endmodule
