// Digital circuit keyboard_control.dig as structural Verilog
module keyboard_control (
  input  _0,
  input  _1,
  input  _2,
  input  _3,
  input  _4,
  input  _5,
  input  _6,
  input  _7,
  input  _8,
  input  _9,
  input  reset,
  input  Alarm_EnableDisable,
  input  Enter,
  input  clrBuffer,
  input  Esc,
  output [3:0] NumCode,
  output NumCodeAvailable,
  output [23:0] NewHHMMSS,
  output [1:0] KeyCode,
  output KeyCodeAvailable
);

  wire or_1_out, or_2_out, or_3_out, priorityencoder_1_any, priorityencoder_2_any;
  wire [1:0] priorityencoder_2_num;
  wire [3:0] priorityencoder_1_num;

  or or_1 (or_1_out, reset, Esc);
  D_FF_AS #(.Bits(4)) d_ff_as_1 (
    .Set(1'b0), .D(NumCode), .C(NumCodeAvailable), .Clr(or_1_out), .Q(NewHHMMSS[3:0]));  // open: nQ
  PriorityEncoder #(.Selector_Bits(4)) priorityencoder_1 (
    .in0(_0), .in1(_1), .in2(_2), .in3(_3), .in4(_4), .in5(_5), .in6(_6), .in7(_7), .in8(_8), .in9(_9),
    .in10(1'b0), .in11(1'b0), .in12(1'b0), .in13(1'b0), .in14(1'b0), .in15(1'b0),
    .num(priorityencoder_1_num), .any(priorityencoder_1_any));
  or or_2 (or_2_out, priorityencoder_1_any, reset);
  // Probe s0 on NewHHMMSS[3:0]
  D_FF_AS #(.Bits(4)) d_ff_as_2 (
    .Set(1'b0), .D(NewHHMMSS[3:0]), .C(NumCodeAvailable), .Clr(or_1_out), .Q(NewHHMMSS[7:4]));  // open: nQ
  Register #(.Bits(4)) register_1 (
    .D(priorityencoder_1_num), .C(priorityencoder_1_any), .en(~NumCodeAvailable), .Q(NumCode));
  // Probe s1 on NewHHMMSS[7:4]
  D_FF_AS #(.Bits(4)) d_ff_as_3 (
    .Set(1'b0), .D(NewHHMMSS[7:4]), .C(NumCodeAvailable), .Clr(or_1_out), .Q(NewHHMMSS[11:8]));  // open: nQ
  JK_FF_AS jk_ff_as_1 (
    .Set(1'b0), .J(1'b1), .C(priorityencoder_1_any), .K(1'b0), .Clr(or_2_out), .Q(NumCodeAvailable));  // open: nQ
  // Probe on NumCodeAvailable
  // Probe s2 on NewHHMMSS[11:8]
  D_FF_AS #(.Bits(4)) d_ff_as_4 (
    .Set(1'b0), .D(NewHHMMSS[11:8]), .C(NumCodeAvailable), .Clr(or_1_out), .Q(NewHHMMSS[15:12]));  // open: nQ
  // Probe s3 on NewHHMMSS[15:12]
  D_FF_AS #(.Bits(4)) d_ff_as_5 (
    .Set(1'b0), .D(NewHHMMSS[15:12]), .C(NumCodeAvailable), .Clr(or_1_out), .Q(NewHHMMSS[19:16]));  // open: nQ
  // Probe s4 on NewHHMMSS[19:16]
  D_FF_AS #(.Bits(4)) d_ff_as_6 (
    .Set(1'b0), .D(NewHHMMSS[19:16]), .C(NumCodeAvailable), .Clr(or_1_out), .Q(NewHHMMSS[23:20]));  // open: nQ
  // Probe on Alarm_EnableDisable
  // Probe s5 on NewHHMMSS[23:20]
  PriorityEncoder #(.Selector_Bits(2)) priorityencoder_2 (
    .in0(1'b0), .in1(Enter), .in2(Esc), .in3(1'b0), .num(priorityencoder_2_num), .any(priorityencoder_2_any));
  or or_3 (or_3_out, clrBuffer, reset);
  Register #(.Bits(2)) register_2 (
    .D(priorityencoder_2_num), .C(priorityencoder_2_any), .en(~KeyCodeAvailable), .Q(KeyCode));
  JK_FF_AS jk_ff_as_2 (
    .Set(1'b0), .J(1'b1), .C(priorityencoder_2_any), .K(1'b0), .Clr(or_3_out), .Q(KeyCodeAvailable));  // open: nQ

  // Notes on the sheet:
  //   New Time
endmodule
